// Logisim project general_purpose_register.circ as structural Verilog: 4 circuits, main circuit main
module main (
);

  wire clock_1_out;
  wire [3:0] rom_1_data;
  wire [7:0] alu_1_result, n8bit_reg_1_regreada, n8bit_reg_1_regreadb;

  Clock clock_1 (.out(clock_1_out));
  _8bit_reg u_8bit_reg_1 (
    .RegWriteEn(1'b1), .RegWriteSel(3'b010), .RegReadA(n8bit_reg_1_regreada), .RegReadSelA(3'b001),
    .RegReadB(n8bit_reg_1_regreadb), .RegReadSelB(3'b010), .data(8'h7), .clk(clock_1_out));
  ROM #(.addrWidth(4), .dataWidth(4)) rom_1 (.addr(4'b1100), .data(rom_1_data), .sel(1'b1));
  alu alu_1 (
    .A(n8bit_reg_1_regreada), .B(n8bit_reg_1_regreadb), .AluOp(rom_1_data), .Result(alu_1_result));  // open: Carry, Zero, Negative

  // Notes on the sheet:
  //   contents of rom_1 (hex, n*v repeats v):
  //   0 1 2 3 4 5 6 7 8 9 a b c d
  //   0: ADD
  //   1: SUB
  //   2: MUL
  //   3: DIV
  //   4: DIV_REM
  //   5: AND
  //   6: OR
  //   7: XOR
  //   8: NAND
  //   9: NOR
  //   10: NOT
  //   11: LOG_LEFT
  //   12: LOG_RIGHT
  //   13: ARITH_LEFT
endmodule

module gp_register (
  input  RegWrite,
  input  [1:0] RegReadSel0,
  input  [1:0] RegWriteSel0,
  input  [1:0] RegReadSel1,
  input  [3:0] RegData,
  input  RegClk,
  input  Rst,
  output [3:0] RegRead0,
  output [3:0] RegRead1
);

  wire demultiplexer_1_out0, demultiplexer_1_out1, demultiplexer_1_out2, demultiplexer_1_out3;
  wire [3:0] register_1_q, register_2_q, register_3_q, register_4_q;

  Demultiplexer #(.select(2)) demultiplexer_1 (
    .out0(demultiplexer_1_out0), .out1(demultiplexer_1_out1), .out2(demultiplexer_1_out2),
    .out3(demultiplexer_1_out3), .in(RegWrite), .sel(RegWriteSel0));  // open: en
  Register #(.width(4)) register_1 (.en(demultiplexer_1_out0), .Q(register_1_q), .clk(RegClk), .clr(Rst));  // open: D
  Register #(.width(4)) register_2 (.D(RegData), .en(demultiplexer_1_out1), .Q(register_2_q), .clk(RegClk), .clr(Rst));
  Register #(.width(4)) register_3 (.D(RegData), .en(demultiplexer_1_out2), .Q(register_3_q), .clk(RegClk), .clr(Rst));
  Register #(.width(4)) register_4 (.D(RegData), .en(demultiplexer_1_out3), .Q(register_4_q), .clk(RegClk), .clr(Rst));
  Multiplexer #(.select(2), .width(4)) multiplexer_1 (
    .in0(register_1_q), .in1(register_2_q), .in2(register_3_q), .in3(register_4_q), .out(RegRead0),
    .sel(RegReadSel0));  // open: en
  Multiplexer #(.select(2), .width(4)) multiplexer_2 (
    .in0(register_1_q), .in1(register_2_q), .in2(register_3_q), .in3(register_4_q), .out(RegRead1),
    .sel(RegReadSel1));  // open: en
endmodule

module _8bit_reg (
  input  [2:0] RegReadSelA,
  input  RegWriteEn,
  input  [2:0] RegWriteSel,
  input  [2:0] RegReadSelB,
  input  [7:0] data,
  input  clk,
  output [7:0] RegReadA,
  output [7:0] RegReadB
);

  wire demultiplexer_1_out0, demultiplexer_1_out1, demultiplexer_1_out2, demultiplexer_1_out3,
       demultiplexer_1_out4, demultiplexer_1_out5, demultiplexer_1_out6;
  wire [7:0] register_1_q, register_2_q, register_3_q, register_4_q, register_5_q, register_6_q, register_7_q;

  Demultiplexer #(.select(3)) demultiplexer_1 (
    .out0(demultiplexer_1_out0), .out1(demultiplexer_1_out1), .out2(demultiplexer_1_out2),
    .out3(demultiplexer_1_out3), .out4(demultiplexer_1_out4), .out5(demultiplexer_1_out5),
    .out6(demultiplexer_1_out6), .in(RegWriteEn), .sel(RegWriteSel));  // open: out7, en
  Register register_1 (.en(demultiplexer_1_out0), .Q(register_1_q), .clk(clk));  // open: D, clr
  Register register_2 (.D(data), .en(demultiplexer_1_out1), .Q(register_2_q), .clk(clk));  // open: clr
  Register register_3 (.D(data), .en(demultiplexer_1_out2), .Q(register_3_q), .clk(clk));  // open: clr
  Register register_4 (.D(data), .en(demultiplexer_1_out3), .Q(register_4_q), .clk(clk));  // open: clr
  Register register_5 (.D(data), .en(demultiplexer_1_out4), .Q(register_5_q), .clk(clk));  // open: clr
  Register register_6 (.D(data), .en(demultiplexer_1_out5), .Q(register_6_q), .clk(clk));  // open: clr
  Register register_7 (.D(data), .en(demultiplexer_1_out6), .Q(register_7_q), .clk(clk));  // open: clr
  Multiplexer #(.select(3), .width(8)) multiplexer_1 (
    .in0(register_1_q), .in1(register_2_q), .in2(register_3_q), .in3(register_4_q), .in4(register_5_q),
    .in5(register_6_q), .in6(register_7_q), .out(RegReadA), .sel(RegReadSelA));  // open: in7, en
  Multiplexer #(.select(3), .width(8)) multiplexer_2 (
    .in0(register_1_q), .in1(register_2_q), .in2(register_3_q), .in3(register_4_q), .in4(register_5_q),
    .in5(register_6_q), .in6(register_7_q), .out(RegReadB), .sel(RegReadSelB));  // open: in7, en
endmodule

module alu (
  input  [7:0] A,
  input  [7:0] B,
  input  [3:0] AluOp,
  output Carry,
  output Zero,
  output Negative,
  output [7:0] Result
);

  wire adder_1_cout, or_2_out, subtractor_1_bout;
  wire [7:0] adder_1_out, and_1_out, divider_1_out, divider_1_rem, multiplier_1_out, nand_1_out, nor_1_out,
       not_1_out, or_1_out, shifter_1_out, shifter_2_out, shifter_3_out, subtractor_1_out, xor_1_out;

  Adder adder_1 (.a(A), .b(B), .out(adder_1_out), .cin(1'b0), .cout(adder_1_cout));
  Subtractor subtractor_1 (.a(A), .b(B), .out(subtractor_1_out), .bin(1'b0), .bout(subtractor_1_bout));
  Multiplier multiplier_1 (.a(A), .b(B), .out(multiplier_1_out), .cin({8{1'b0}}));  // open: cout
  Divider divider_1 (.a(A), .b(B), .out(divider_1_out), .upper({8{1'b0}}), .rem(divider_1_rem));
  assign and_1_out = A & B;  // AND_Gate and_1, 8 bits wide
  assign or_1_out = A | B;  // OR_Gate or_1, 8 bits wide
  assign xor_1_out = A ^ B;  // XOR_Gate xor_1, 8 bits wide
  assign nand_1_out = ~(A & B);  // NAND_Gate nand_1, 8 bits wide
  assign nor_1_out = ~(A | B);  // NOR_Gate nor_1, 8 bits wide
  assign not_1_out = ~A;  // NOT_Gate not_1, 8 bits wide
  Shifter shifter_1 (.in(A), .\dist (B[2:0]), .out(shifter_1_out));
  Shifter #(.shift("lr")) shifter_2 (.in(A), .\dist (B[2:0]), .out(shifter_2_out));
  Shifter #(.shift("ar")) shifter_3 (.in(A), .\dist (B[2:0]), .out(shifter_3_out));
  Multiplexer #(.select(4)) multiplexer_1 (
    .in0(adder_1_cout), .in1(subtractor_1_bout), .in2(1'b0), .in3(1'b0), .in4(1'b0), .in5(1'b0), .in6(1'b0),
    .in7(1'b0), .in8(1'b0), .in9(1'b0), .in10(1'b0), .in11(1'b0), .in12(1'b0), .in13(1'b0), .in14(1'b0),
    .in15(1'b0), .out(Carry), .sel(AluOp));  // open: en
  Multiplexer #(.select(4), .width(8)) multiplexer_2 (
    .in0(adder_1_out), .in1(subtractor_1_out), .in2(multiplier_1_out), .in3(divider_1_out),
    .in4(divider_1_rem), .in5(and_1_out), .in6(or_1_out), .in7(xor_1_out), .in8(nand_1_out), .in9(nor_1_out),
    .in10(not_1_out), .in11(shifter_1_out), .in12(shifter_2_out), .in13(shifter_3_out),
    .out({Negative, Result[6:0]}), .sel(AluOp));  // open: in14, in15, en
  or or_2 (or_2_out, Result[0], Result[1], Result[2], Result[3], Result[4], Result[5], Result[6], Negative);
  not not_2 (Zero, or_2_out);

  assign Result[7] = Negative;
endmodule
