// Logisim project tff.circ as structural Verilog
module main (
  input  in_1,
  input  in_2
);

  wire and_1_out, and_2_out, and_3_out, and_4_out, and_5_out, and_6_out, and_7_out, and_8_out, clock_1_out,
       not_1_out, or_1_out, or_2_out, or_3_out, or_4_out, t_ff_1_q, t_ff_1_qn, t_ff_2_q, t_ff_2_qn, t_ff_3_q,
       t_ff_3_qn, t_ff_4_q, t_ff_4_qn;

  Clock clock_1 (.out(clock_1_out));
  T_Flip_Flop t_ff_1 (.clk(clock_1_out), .T(in_1), .Q(t_ff_1_q), .Qn(t_ff_1_qn));  // open: preset, reset, en
  not not_1 (not_1_out, in_2);
  and and_1 (and_1_out, not_1_out, t_ff_1_q);
  and and_2 (and_2_out, t_ff_1_qn, in_2);
  or or_1 (or_1_out, and_1_out, and_2_out);
  LED led_1 (.in(or_1_out));
  T_Flip_Flop t_ff_2 (.clk(clock_1_out), .T(or_1_out), .Q(t_ff_2_q), .Qn(t_ff_2_qn));  // open: preset, reset, en
  and and_3 (and_3_out, and_1_out, t_ff_2_q);
  and and_4 (and_4_out, t_ff_2_qn, and_2_out);
  T_Flip_Flop t_ff_3 (.clk(clock_1_out), .T(or_2_out), .Q(t_ff_3_q), .Qn(t_ff_3_qn));  // open: preset, reset, en
  or or_2 (or_2_out, and_3_out, and_4_out);
  LED led_2 (.in(or_2_out));
  and and_5 (and_5_out, and_3_out, t_ff_3_q);
  and and_6 (and_6_out, t_ff_3_qn, and_4_out);
  or or_3 (or_3_out, and_5_out, and_6_out);
  LED led_3 (.in(or_3_out));
  T_Flip_Flop t_ff_4 (.clk(clock_1_out), .T(or_3_out), .Q(t_ff_4_q), .Qn(t_ff_4_qn));  // open: preset, reset, en
  and and_7 (and_7_out, and_5_out, t_ff_4_q);
  and and_8 (and_8_out, t_ff_4_qn, and_6_out);
  or or_4 (or_4_out, and_7_out, and_8_out);
  LED led_4 (.in(or_4_out));
endmodule
